# Fritzing sketch BlinkyButton (saved by Fritzing 0.9.2b)
circuit board: 8.46667cm x 5.64444cm
stripboards: 1

parts:
  Part1 = Photon
  CHARGER1 = USB_LiIon_LiPoly_Charger_v1.2
  U1 = Vibration Motor- ROB-08449 [package=vibe-motor-10mm]
  R2 = Resistor [tolerance=±10% resistance=33k package=THT]
  R1 = Resistor [tolerance=±10% resistance=47k package=THT]
  U2 = LIPO-2000mAh [package=lipo-2000]
  R3 = Resistor [tolerance=±10% resistance=10k package=THT]
  S1 = Pushbutton [package="[THT]"]
  NEOPIXEL1 = Neopixel Strip -- White (60/m)

nets:
  N1: Part1.A5, R2.Pin_1, R1.Pin_1
  GND: Part1.TX, Part1.GND, CHARGER1.load_minus_2, NEOPIXEL1.GND
  VIN: Part1.VIN, CHARGER1.load_plus_2, NEOPIXEL1.+5V
  N2: Part1.D3, NEOPIXEL1.DI
  N3: Part1.D4, R3.Pin_1, S1.Pin_1, S1.Pin_2
  N4: Part1.D5, U1.+
  N5: CHARGER1.batt_minus_1, U2.-
  N6: CHARGER1.batt_plus_1, U2.+
  N7: U1.-, R1.Pin_0, R3.Pin_0
  N8: R2.Pin_0, S1.Pin_3, S1.Pin_4

custom parts:
  Neopixel Strip -- White (60/m): Neopixel Strip, White, 60 pixels per meter.
